// Digital circuit lab10.dig as structural Verilog
module lab10 (
  input  [8:0] N,
  input  reset,
  input  start,
  input  clock,
  output done,
  output [7:0] displayout,
  output [15:0] clockcount,
  output valid
);

  wire and_2_out, and_3_out, and_4_out, clk, comparator_1_eq, comparator_2_gt, comparator_3_gt,
       comparator_4_eq, comparator_5_eq, \end , multiplexer_2_out, multiplexer_5_out, multiplexer_9_out,
       multiplexer_12_out, not_1_out, not_2_out, or_1_out, or_2_out, or_3_out;
  wire [7:0] add_2_s, multiplexer_3_out, multiplexer_4_out, multiplexer_6_out, out, ROMFILE_d;
  wire [8:0] add_1_s, add_4_s, add_5_s, d_ff_1_q, d_ff_5_q, d_ff_6_q, in, multiplexer_1_out,
       multiplexer_8_out, multiplexer_10_out, multiplexer_13_out, n_1, num, sub_2_s;
  wire [15:0] add_3_s, multiplexer_7_out;

  Add #(.Bits(9)) add_1 (.a(d_ff_1_q), .b(9'h1), .c_i(1'b0), .s(add_1_s));  // open: c_o
  and and_1 (clk, start, clock);
  Multiplexer #(.Bits(9)) multiplexer_1 (.sel(reset), .in_0(add_1_s), .in_1({9{1'b0}}), .out(multiplexer_1_out));
  Multiplexer multiplexer_2 (.sel(\end ), .in_0(clk), .in_1(1'b0), .out(multiplexer_2_out));
  Multiplexer #(.Bits(8)) multiplexer_3 (.sel(\end ), .in_0({8{1'b0}}), .in_1(8'h1), .out(multiplexer_3_out));
  D_FF #(.Bits(9)) d_ff_1 (.D(multiplexer_1_out), .C(multiplexer_2_out), .Q(d_ff_1_q));  // open: nQ
  Add #(.Bits(8)) add_2 (.a(out), .b(multiplexer_3_out), .c_i(1'b0), .s(add_2_s));  // open: c_o
  Multiplexer #(.Bits(8)) multiplexer_4 (.sel(reset), .in_0(add_2_s), .in_1({8{1'b0}}), .out(multiplexer_4_out));
  Comparator #(.Bits(9)) comparator_1 (.a(num), .b({9{1'b0}}), .eq(comparator_1_eq));  // open: gt, lt
  Sub #(.Bits(9)) sub_1 (.a(N), .b(9'h1), .c_i(1'b0), .s(n_1));  // open: c_o
  and and_2 (and_2_out, comparator_1_eq, clk);
  ROM #(.AddrBits(9), .isProgramMemory("true"), .Bits(8)) ROMFILE (.A(d_ff_1_q), .sel(1'b1), .D(ROMFILE_d));
  Add #(.Bits(16)) add_3 (.a(clockcount), .b({16{1'b0}}), .c_i(1'b0), .s(add_3_s));  // open: c_o
  Comparator #(.Bits(9)) comparator_2 (.a(d_ff_1_q), .b(n_1), .gt(comparator_2_gt));  // open: eq, lt
  Multiplexer multiplexer_5 (.sel(\end ), .in_0(clk), .in_1(1'b0), .out(multiplexer_5_out));
  D_FF #(.Bits(8)) d_ff_2 (.D(multiplexer_4_out), .C(and_2_out), .Q(out));  // open: nQ
  D_FF d_ff_3 (.D(comparator_2_gt), .C(or_1_out), .Q(\end ));  // open: nQ
  or or_1 (or_1_out, multiplexer_5_out, reset);
  Multiplexer #(.Bits(8)) multiplexer_6 (.sel(\end ), .in_0(ROMFILE_d), .in_1(out), .out(multiplexer_6_out));
  Multiplexer #(.Bits(16)) multiplexer_7 (.sel(done), .in_0(add_3_s), .in_1(clockcount), .out(multiplexer_7_out));
  not not_1 (not_1_out, reset);
  and and_3 (and_3_out, clk, not_1_out);
  Add #(.Bits(9)) add_4 (.a(d_ff_6_q), .b(9'h1), .c_i(1'b0), .s(add_4_s));  // open: c_o
  Multiplexer #(.Bits(9)) multiplexer_8 (.sel(reset), .in_0(add_4_s), .in_1({9{1'b0}}), .out(multiplexer_8_out));
  Comparator #(.Bits(9)) comparator_3 (.a(num), .b({9{1'b0}}), .gt(comparator_3_gt));  // open: eq, lt
  D_FF #(.Bits(16)) d_ff_4 (.D(multiplexer_7_out), .C(clk), .Q(clockcount));  // open: nQ
  RAMDualPort #(.AddrBits(8), .Bits(9)) RAM (
    .A(multiplexer_6_out), .Din(in), .str(1'b1), .C(and_3_out), .ld(1'b1), .D(num));
  or or_2 (or_2_out, reset, multiplexer_12_out);
  Multiplexer multiplexer_9 (.sel(\end ), .in_0(1'b0), .in_1(comparator_3_gt), .out(multiplexer_9_out));
  D_FF #(.Bits(9)) d_ff_5 (.D(multiplexer_8_out), .C(or_2_out), .Q(d_ff_5_q));  // open: nQ
  Sub #(.Bits(9)) sub_2 (.a(num), .b(9'h1), .c_i(1'b0), .s(sub_2_s));  // open: c_o
  Comparator #(.Bits(9)) comparator_4 (.a(num), .b({9{1'b0}}), .eq(comparator_4_eq));  // open: gt, lt
  and and_4 (and_4_out, multiplexer_9_out, not_2_out);
  not not_2 (not_2_out, clk);
  Add #(.Bits(9)) add_5 (.a(num), .b(9'h1), .c_i(1'b0), .s(add_5_s));  // open: c_o
  Multiplexer #(.Bits(9)) multiplexer_10 (
    .sel(comparator_4_eq), .in_0(sub_2_s), .in_1({9{1'b0}}), .out(multiplexer_10_out));
  Comparator #(.Bits(9)) comparator_5 (.a(d_ff_6_q), .b(d_ff_5_q), .eq(comparator_5_eq));  // open: gt, lt
  Multiplexer #(.Bits(9)) multiplexer_11 (.sel(\end ), .in_0(add_5_s), .in_1(multiplexer_10_out), .out(in));
  not not_3 (valid, comparator_5_eq);
  D_FF #(.Bits(9)) d_ff_6 (.D(d_ff_5_q), .C(~clk), .Q(d_ff_6_q));  // open: nQ
  Multiplexer multiplexer_12 (.sel(done), .in_0(and_4_out), .in_1(1'b0), .out(multiplexer_12_out));
  or or_3 (or_3_out, valid, done);
  Multiplexer #(.Bits(9)) multiplexer_13 (.sel(done), .in_0(d_ff_6_q), .in_1(n_1), .out(multiplexer_13_out));
  RAMDualPort #(.AddrBits(9), .isProgramMemory("true"), .Bits(8)) RAM_2 (
    .A(multiplexer_13_out), .Din(out), .str(multiplexer_12_out), .C(multiplexer_12_out), .ld(or_3_out),
    .D(displayout));
  Comparator #(.Bits(9)) comparator_6 (.a(N), .b(d_ff_6_q), .eq(done));  // open: gt, lt
  Seven_Seg_Hex seven_seg_hex_1 (.d(displayout[7:4]), .dp(1'b0));
  Seven_Seg_Hex seven_seg_hex_2 (.d(displayout[3:0]), .dp(1'b0));

  // Notes on the sheet:
  //   clock: Hz: 5
  //   contents of ROMFILE (hex, n*v repeats v):
  //   10,2,3,a,10
endmodule
